# Fritzing sketch teenyGPS (saved by Fritzing 0.8.7b)
circuit board: 8.46667cm x 5.64444cm
breadboards: 1

parts:
  Teensy1 = Teensy 3.0
  S1 = Pushbutton [package=THT]
  S2 = Pushbutton [package=THT]
  S3 = Pushbutton [package=THT]
  S4 = Pushbutton [package=THT]
  S5 = Pushbutton [package=THT]
  S6 = Pushbutton [package=THT]
  S7 = Pushbutton [package=THT]
  S8 = Pushbutton [package=THT]
  S9 = Pushbutton [package=THT]
  S10 = Pushbutton [package=THT]
  S11 = Pushbutton [package=THT]
  S12 = Pushbutton [package=THT]
  RE1 = Rotary Encoder [package=THT]
  RE2 = Rotary Encoder [package=THT]
  S13 = Pushbutton [package=THT]

nets:
  N1: Teensy1.GND, S1.leg0, S2.leg0, S3.leg0, S4.leg0, S5.leg0, S6.leg0, S7.leg0, S8.leg0, S9.leg0, S10.leg0, S11.leg0, S12.leg0, RE1.EncoderPinC, RE2.EncoderPinC, S13.leg0
  N2: Teensy1.D3, RE1.EncoderPinA
  N3: Teensy1.D4, RE1.EncoderPinB
  N4: Teensy1.D5, RE2.EncoderPinA
  N5: Teensy1.D6, RE2.EncoderPinB
  N6: Teensy1.D9, S13.leg1
  N7: Teensy1.D10, S12.leg1
  N8: Teensy1.D11, S11.leg1
  N9: Teensy1.D12, Teensy1.VBat, Teensy1.3V3, S10.leg1
  N10: Teensy1.Program, Teensy1.Reset, Teensy1.D13
  N11: Teensy1.A0/D14, S1.leg1
  N12: Teensy1.A1/D15, S2.leg1
  N13: Teensy1.A2/D16, S3.leg1
  N14: Teensy1.A3/D17, S4.leg1
  N15: Teensy1.A4/D18, S5.leg1
  N16: Teensy1.A5/D19, S6.leg1
  N17: Teensy1.A6/D20, S7.leg1
  N18: Teensy1.A7/D21, Teensy1.A11, S8.leg1
  N19: Teensy1.A8/D22, Teensy1.A10, S9.leg1
  N20: Teensy1.A9/D23, Teensy1.AREF
  N21: Teensy1.AGND, Teensy1.VUSB

notes:
  BUTTONS FOR GPS
